# Fritzing sketch capstone fritzing (saved by Fritzing 1.0.2b)
breadboards: 3

parts:
  Breadboard5 = Breadboard Split Power
  A1 = Particle - Photon2
  Breadboard4 = Breadboard Split Power
  OLED_I2C1 = OLED 128x64 I2C Monochrome Display
  SENS1 = SoilWatch 10
  M1 = DC Motor [voltage_(max)=6V voltage_(min)=3V]
  Relay1 = Relay - 6 pins [package="DIP (Dual Inline) [THT]"]
  Relay2 = Relay - 6 pins [package="DIP (Dual Inline) [THT]"]
  M2 = BMP280
  Water_Level_Sensor1 = Water Level Sensor
  S1 = Round Pushbutton
  Piezoelectric_Sensor1 = Piezoelectric Sensor
  LED1 = LED - 5mm [color="Red (633nm)" current=0.030A package="5 mm [THT]"]

nets:
  VCC: Breadboard5.pin4Y, Breadboard5.pin15Y, Breadboard5.pin17Y, Breadboard5.pin29Y, A1.Pin_2, Breadboard4.pin3Y, Breadboard4.pin6Y, Breadboard4.pin15Y, Breadboard4.pin18Y, Breadboard4.pin21Y, Breadboard4.pin29Y, OLED_I2C1.VDD, SENS1.VCC, Relay1.VCC, Relay2.VCC, M2.VIN, Piezoelectric_Sensor1.VCC
  GND: Breadboard5.pin4Z, Breadboard5.pin11Z, Breadboard5.pin28Z, A1.Pin_4, Breadboard4.pin3Z, Breadboard4.pin8Z, Breadboard4.pin20Z, Breadboard4.pin29Z, OLED_I2C1.GND, SENS1.GND, Relay1.GND, Relay2.GND, M2.GND, Water_Level_Sensor1.GND, S1.leg1, Piezoelectric_Sensor1.GND
  N1: A1.Pin_5, SENS1.OUT
  N2: A1.Pin_11, Water_Level_Sensor1.SIG
  N3: A1.Pin_13, Relay1.IN
  N4: A1.Pin_17, OLED_I2C1.SDA, M2.SDA
  N5: A1.Pin_18, OLED_I2C1.SCK, M2.SCL
  N6: A1.Pin_24, A1.Pin_36, Relay2.IN
  N7: A1.Pin_26, Water_Level_Sensor1.VCC
  N8: A1.Pin_27, S1.leg0
  N9: M1.pin_1, Relay2.COM
  N10: M1.pin_2, Relay2.ON
  N11: Relay1.COM, LED1.cathode
  N12: Relay1.ON, LED1.anode

custom parts:
  Breadboard Split Power: A custom 6 pin per group power supply strip where the top row (ground) is all bussed together and the bottom row (+V) is split in two groups of 12 pins. This version is modified to be a loadable part and was rescaled to be on the standard 1px = 1thou grid with the size set in inches
  Particle - Photon2: The Photon 2 is a microcontroller and Wi-Fi networking developed by particle. Features: 802.11a/b/g/n Wi-Fi, 2.4 GHz and 5 GHz Integrated PCB antenna Integrated U.FL connector for external antenna Integrated RF switch BLE 5 using same antenna as Wi-Fi Realtek RTL8721DM MCU ARM Cortex M33 CPU, 200 MHz 2048 KB (2 MB) user application maximum size 3072 KB (3 MB) of RAM available to user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
  SoilWatch 10: SoilWatch 10 - Capacitive soil moisture sensor
  Relay - 6 pins: A DIP stand-in part for whatever IC you want. With 6 pins on a 900mil dual inline package (DIP) footprint.
  BMP280: Temperature Humidity Barometric presure Sensor, I2C
  Water Level Sensor: A water level sensor. This sensor operates at 3V to 5V. The Sig (signal) pin outputs an analogue signal that is in proportion to the amount of water in contact with the sensor.
  Piezoelectric Sensor: Piezoelectric sensor.
